// Logisim project automatLebedev3v2.circ as structural Verilog: 1 circuit, main circuit main
module main (
  input  [7:0] in_1,
  input  [3:0] in_2,
  output [7:0] out_3
);

  wire C, CHCK, CT_0, LD_AB, LD_Ost1, LD_Ost2, not_1_out, not_2_out, pull_resistor_1_node, R0, RST, SH_B,
       shift_register_1_out, shift_register_2_out, STEP;
  wire [2:0] counter_1_q, multiplexer_1_out, register_1_q, rom_1_data;
  wire [4:0] adder_1_out, multiplexer_3_out, not_3_out, Ost, register_2_q, RGR_INP, shift_register_2_q0;
  wire [13:3] rom_1_data_2;

  Button button_1 (.out(C));
  Button button_2 ();  // open: out
  Pull_Resistor pull_resistor_1 (.node(pull_resistor_1_node));
  LED led_1 (.in(R0));
  Multiplexer #(.width(3)) multiplexer_1 (
    .in0(rom_1_data), .in1(rom_1_data_2[5:3]), .out(multiplexer_1_out), .sel(CT_0));  // open: en
  Shift_Register #(.length(5)) shift_register_1 (
    .shift(SH_B), .in(1'b0), .clk(C), .out(shift_register_1_out), .load(LD_AB), .clr(RST), .d0(in_1[0]),
    .d1(in_1[1]), .d2(in_1[2]), .d3(in_1[3]), .d4(1'b0));  // open: q0, q1, q2, q3, q4
  Register #(.width(3)) register_1 (.D(multiplexer_1_out), .Q(register_1_q), .clk(C));  // open: en, clr
  Shift_Register #(.length(5)) shift_register_2 (
    .shift(SH_B), .in(shift_register_1_out), .clk(C), .out(shift_register_2_out), .load(LD_Ost1), .clr(RST),
    .d0(Ost[0]), .q0(shift_register_2_q0[0]), .d1(Ost[1]), .q1(shift_register_2_q0[1]), .d2(Ost[2]),
    .q2(shift_register_2_q0[2]), .d3(Ost[3]), .q3(shift_register_2_q0[3]), .d4(Ost[4]),
    .q4(shift_register_2_q0[4]));
  ROM #(.addrWidth(3), .dataWidth(14)) rom_1 (
    .addr(register_1_q),
    .data({rom_1_data_2[13], CHCK, STEP, SH_B, RST, LD_Ost2, LD_Ost1, LD_AB, rom_1_data_2[5:3], rom_1_data}));  // open: sel
  not not_1 (not_1_out, shift_register_2_out);
  Shift_Register #(.length(5)) shift_register_3 (
    .shift(SH_B), .in(not_1_out), .clk(C), .clr(RST));  // open: out, load, d0, q0, d1, q1, d2, q2, d3, q3, d4, q4
  Multiplexer #(.width(5)) multiplexer_2 (
    .in0(RGR_INP), .in1({1'b0, in_1[7:4]}), .out(Ost), .sel(LD_Ost2));  // open: en
  not not_2 (not_2_out, LD_AB);
  Register #(.width(5)) register_2 (.D({1'b0, in_2}), .en(LD_AB), .Q(register_2_q), .clk(C), .clr(RST));
  assign not_3_out = ~register_2_q;  // NOT_Gate not_3, 5 bits wide
  Adder #(.width(5)) adder_1 (.a(not_3_out), .b(5'b00001), .out(adder_1_out));  // open: cin, cout
  Counter #(.width(3), .max('h4)) counter_1 (
    .load(1'b1), .D(3'b101), .count(not_2_out), .Q(counter_1_q), .clk(STEP), .clr(RST));  // open: carry
  Multiplexer #(.width(5)) multiplexer_3 (
    .in0(adder_1_out), .in1(register_2_q), .out(multiplexer_3_out), .sel(shift_register_2_q0[4]));  // open: en
  D_Flip_Flop d_ff_1 (.clk(C), .D(CHCK), .Q(R0), .reset(RST));  // open: Qn, preset, en
  nor nor_1 (CT_0, counter_1_q[0], counter_1_q[1], counter_1_q[2]);
  Adder #(.width(5)) adder_2 (.a(multiplexer_3_out), .b(shift_register_2_q0), .out(RGR_INP));  // open: cin, cout

  // Other names for the same wires on the sheet: input1[7:0] = in_1; input2[3:0] = in_2

  // Notes on the sheet:
  //   C
  //   contents of rom_1 (hex, n*v repeats v):
  //   209 9d2
endmodule
